# Fritzing sketch analyzer (saved by Fritzing 0.9.3b)
breadboards: 1

parts:
  Part2 = Arduino Uno (Rev3) - ICSP
  U2 = LCD-16X2 [package=lcd-16x2]
  R4 = Trimmer Potentiometer [maximum_resistance=10kΩ package=THT]  # not connected
  R5 = Resistor [tolerance=±5% resistance=220 package="0805 [SMD]"]
  DHT1 = DHT11 Humitidy and Temperature Sensor (3 pins)
  Part3 = Soil Moisture Sensor

nets:
  N1: Part2.A0, DHT1.GND
  N2: Part2.A1, Part3.SIG
  N3: Part2.D12/MISO, U2.E
  N4: Part2.D13/SCK, U2.RS
  N5: Part2.D2, U2.DB7
  N6: Part2.D3_PWM, U2.DB6
  N7: Part2.D4, U2.DB5
  N8: Part2.D5_PWM, U2.DB4
  VDD: Part2.5V, U2.VDD, R5.Pin_0, DHT1.VDD, Part3.VCC
  GND: Part2.GND, U2.VSS, U2.R_W, U2.K, DHT1.DATA, Part3.GND
  N9: U2.A, R5.Pin_1

notes:
  220 Ohm Resistor
  Master Arduino

custom parts:
  DHT11 Humitidy and Temperature Sensor (3 pins): DHT11 Humidity and Temperature Sensor (3 pins) from the design created by John De Cristofaro for Adafruit Industries.
