# Fritzing sketch outlet (saved by Fritzing 0.9.3b)

parts:
  Part1 = KY-019 5V Relay Module [package="Breakout board"]
  U1 = Power Outlet [chip_label=IC package="SIP (Single Inline) [THT]"]

nets:
  N1: Part1.NO, U1.hot2

notes:
  Power Cable with Plug
  Performer Arduino
  Desk Lamp (plug in)
  Activates on High

custom parts:
  KY-019 5V Relay Module: KY-019 5V Relay module, used to control AC circuits.
  Power Outlet: A standard power outlet. Silver screws are neutral, brass screws are hot. Green screw is ground.
