# Fritzing sketch performer (saved by Fritzing 0.9.3b)
breadboards: 1

parts:
  Part1 = Arduino Uno (Rev3) - ICSP
  S1 = Pushbutton [package="[THT]"]
  R1 = Resistor [tolerance=±5% resistance=220 package="0805 [SMD]"]

nets:
  N1: Part1.5V, S1.Pin_3, S1.Pin_4
  N2: Part1.D7, S1.Pin_1, S1.Pin_2, R1.Pin_1
  N3: Part1.GND, R1.Pin_0

notes:
  Master Arduino
  5v Relay
