# Fritzing sketch allTogether (saved by Fritzing 0.9.3b)
breadboards: 3

parts:
  Part2 = Arduino Uno (Rev3) - ICSP
  S2 = Pushbutton [package="[THT]"]
  U2 = LCD-16X2 [package=lcd-16x2]
  R4 = Trimmer Potentiometer [maximum_resistance=10kΩ package=THT]  # not connected
  R5 = Resistor [tolerance=±5% resistance=220 package="0805 [SMD]"]
  R6 = Resistor [tolerance=±5% resistance=220 package="0805 [SMD]"]
  Part4 = Arduino Uno (Rev3) - ICSP
  U3 = LCD-16X2 [package=lcd-16x2]
  R7 = Trimmer Potentiometer [maximum_resistance=10kΩ package=THT]  # not connected
  R8 = Resistor [tolerance=±5% resistance=220 package="0805 [SMD]"]
  DHT2 = DHT11 Humitidy and Temperature Sensor (3 pins)
  Part5 = Soil Moisture Sensor
  Part6 = Arduino Uno (Rev3) - ICSP
  S3 = Pushbutton [package="[THT]"]
  R9 = Resistor [tolerance=±5% resistance=220 package="0805 [SMD]"]
  Part7 = KY-019 5V Relay Module [package="Breakout board"]
  U4 = Power Outlet [chip_label=IC package="SIP (Single Inline) [THT]"]

nets:
  N1: Part2.A4/SDA, Part4.A4/SDA, Part6.A4/SDA
  N2: Part2.A5/SCL, Part4.A5/SCL, Part6.A5/SCL
  N3: Part2.D12/MISO, U2.E
  N4: Part2.D13/SCK, U2.RS
  N5: Part2.D2, U2.DB7
  N6: Part2.D3_PWM, U2.DB6
  N7: Part2.D4, U2.DB5
  N8: Part2.D5_PWM, U2.DB4
  N9: Part2.D7, S2.Pin_1, S2.Pin_2, R6.Pin_1
  N10: S2.Pin_3, S2.Pin_4, U2.VDD, R5.Pin_0, R6.Pin_0
  GND: U2.VSS, U2.R_W, U2.K, Part4.GND, U3.VSS, U3.R_W, U3.K, DHT2.DATA, Part5.GND, Part6.GND, R9.Pin_0, Part7.-
  N11: U2.A, R5.Pin_1
  N12: Part4.A0, DHT2.GND
  N13: Part4.A1, Part5.SIG
  N14: Part4.D12/MISO, U3.E
  N15: Part4.D2, U3.DB7
  N16: Part4.D3_PWM, U3.DB6
  N17: Part4.D4, U3.DB5
  N18: Part4.D5_PWM, U3.DB4
  VDD: Part4.5V, U3.VDD, R8.Pin_0, DHT2.VDD, Part5.VCC
  N19: U3.A, R8.Pin_1
  N20: Part6.D4, Part7.S
  N21: Part6.D7, S3.Pin_1, S3.Pin_2, R9.Pin_1
  N22: Part6.5V, S3.Pin_3, S3.Pin_4, Part7.+
  N23: Part7.NO, U4.hot2

notes:
  10k Ohm Resistor
  220 Ohm Resistor
  Power Cable with Plug
  Desk Lamp (plug in)
  Activates on High
  Master Arduino
  Performer Arduino
  Analyzer Arduino

custom parts:
  DHT11 Humitidy and Temperature Sensor (3 pins): DHT11 Humidity and Temperature Sensor (3 pins) from the design created by John De Cristofaro for Adafruit Industries.
  KY-019 5V Relay Module: KY-019 5V Relay module, used to control AC circuits.
  Power Outlet: A standard power outlet. Silver screws are neutral, brass screws are hot. Green screw is ground.
