# Fritzing sketch masterController (saved by Fritzing 0.9.3b)
breadboards: 1

parts:
  Part1 = Arduino Uno (Rev3) - ICSP
  S1 = Pushbutton [package="[THT]"]
  U1 = LCD-16X2 [package=lcd-16x2]
  R1 = Trimmer Potentiometer [maximum_resistance=10kΩ package=THT]  # not connected
  R2 = Resistor [tolerance=±5% resistance=220 package="0805 [SMD]"]
  R3 = Resistor [tolerance=±5% resistance=220 package="0805 [SMD]"]

nets:
  N1: Part1.D12/MISO, U1.E
  N2: Part1.D13/SCK, U1.RS
  GND: Part1.GND, U1.VSS, U1.R_W, U1.K
  N3: Part1.D2, U1.DB7
  N4: Part1.D3_PWM, U1.DB6
  N5: Part1.D4, U1.DB5
  N6: Part1.D5_PWM, U1.DB4
  N7: Part1.D7, S1.Pin_1, S1.Pin_2, R2.Pin_1
  5V: Part1.5V, S1.Pin_3, S1.Pin_4, U1.VDD, R2.Pin_0, R3.Pin_0
  N8: U1.A, R3.Pin_1

notes:
  220 Ohm Resistor
  10k Ohm Resistor
  Analyzer Arduino
  Performer Arduino
